# Fritzing sketch CI_CAS_NightLife16_v1 (saved by Fritzing 0.9.2b)
circuit board: 3.76715cm x 2.06939cm
breadboards: 1

parts:
  Part1 = Photon
  JP1 = Header 1 [package=1x01_offset]  # not connected
  JP2 = Header 1 [package=1x01_offset]
  JP3 = Header 1 [package=1x01_offset]
  JP4 = Header 1 [package=1x01_offset]
  JP5 = Header 1 [package=1x01_offset]

nets:
  N1: Part1.A0, JP2.1
  N2: Part1.VIN, JP3.1, JP4.1
  N3: Part1.GND, JP5.1
